# Fritzing sketch force-sensor (saved by Fritzing 0.7.12b)
breadboards: 1

parts:
  Arduino1 = Arduino
  R1 = Trimmer Potentiometer [maximum_resistance=10kΩ package=THT]

nets:
  N1: Arduino1.+5V, R1.leg2
  N2: Arduino1.GND, R1.leg1
  N3: Arduino1.A0, R1.wiper
